# Fritzing sketch Basic-Fritzing (saved by Fritzing 0.9.3b)

parts:
  Part1 = Adafruit Stereo 3W Speaker Bonnet [part_number="Adafruit #"]
  Raspberry_Pi_Zero1 = Raspberry Pi Zero
  SP1 = SPEAKER [package=pcb_mount_speaker]
  SP2 = SPEAKER [package=pcb_mount_speaker]
  Part2 = sx1509 breakout
  Part3 = sx1509 breakout

nets:
  N1: Part1.SDA, Part2.SDA, Part3.SDA
  N2: Part1.SCL, Part2.SCL, Part3.SCL
  N3: Part1.5.0V, Raspberry_Pi_Zero1.5V
  GND: Part1.GND, Raspberry_Pi_Zero1.GND, Part2.GND, Part3.GND
  N4: Part1.DIN, Raspberry_Pi_Zero1.GPIO21
  N5: Part1.RIGHT-, SP2.+
  N6: Part1.RIGHT+, SP2.-
  N7: Part1.LEFT+, SP1.-
  N8: Part1.LEFT-, SP1.+
  3V3: Raspberry_Pi_Zero1.3v3, Raspberry_Pi_Zero1.3V3, Part2.3.3V, Part3.3.3V

notes:
  These branch out to LEDs and stuff

custom parts:
  Adafruit Stereo 3W Speaker Bonnet: Hey Mr. DJ! Turn up that Raspberry Pi mix to the max with this cute 3W Stereo Amplifier Bonnet for Raspberry Pi. (It's not big enough to be an official HAT, so we called it a bonnet, you see?) It's the exact same size as a Raspberry Pi Zero but works with any and all Raspberry Pi computers with a 2x20 connector - A+, B+, Zero, Pi 2, Pi 3, etc. This Bonnet uses I2S a digital sound standard, so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
